# Fritzing sketch mobile-main (saved by Fritzing 0.9.3b)
circuit board: 12cm x 14cm
breadboards: 1

parts:
  IC1 = DIP - 14 pins [chip_label=IC package="DIP (Dual Inline) [THT]"]
  LED1 = LED - 3mm [color="Red (633nm)" package="3 mm [THT]"]
  LED2 = LED - 3mm [color="Red (633nm)" package="3 mm [THT]"]
  LED3 = LED - 3mm [color="Red (633nm)" package="3 mm [THT]"]
  LED4 = LED - 3mm [color="Red (633nm)" package="3 mm [THT]"]
  LED5 = LED - 3mm [color="Red (633nm)" package="3 mm [THT]"]
  LED6 = LED - 3mm [color="Red (633nm)" package="3 mm [THT]"]
  R7 = Resistor [tolerance=±5% resistance=470 package=THT]
  R8 = Resistor [tolerance=±5% resistance=470 package=THT]
  R9 = Resistor [tolerance=±5% resistance=470 package=THT]
  R10 = Resistor [tolerance=±5% resistance=470 package=THT]
  R11 = Resistor [tolerance=±5% resistance=470 package=THT]
  Part1 = Arduino Mega 2560 (Rev3)
  J8 = Camdenboss CTB0158-2 [part_number=CTB0158-2 package=THT]
  J9 = Camdenboss CTB0158-2 [part_number=CTB0158-2 package=THT]
  L293D1 = L293D [package=THT]
  J10 = Voltage Reguator [form="♀ (female)" package=THT]
  S6 = SPST Switch [package=switch-spdt]
  S9 = SWITCH-MOMENTARY-2 [package=tactile-pth-12mm]
  LED7 = LED - 3mm [color="Red (633nm)" package="3 mm [THT]"]
  R13 = Resistor [tolerance=±5% resistance=470 package=THT]
  S10 = Momentary Switch [package=ksa_sealed_tac_switch]
  LCD1 = LCD screen
  R16 = Resistor [tolerance=±5% resistance=220 package=THT]
  J12 = female pin header, 2 pins [form="♀ (female)"]
  S11 = SWITCH-MOMENTARY-2 [package=tactile-pth-12mm]
  S8 = Momentary Switch [package=ksa_sealed_tac_switch]
  S12 = Momentary Switch [package=ksa_sealed_tac_switch]
  IC2 = DIP - 14 pins [chip_label=IC package="DIP (Dual Inline) [THT]"]
  J13 = female pin header, 8 pins [form="♀ (female)"]
  J15 = HC-12 [form="♀ (female)" package=THT]
  J16 = female pin header, 4 pins [form="♀ (female)"]
  J17 = female pin header, 2 pins [form="♀ (female)"]
  J18 = Camdenboss CTB0158-2 [part_number=CTB0158-2 package=THT]
  R1 = Trimmer Potentiometer [maximum_resistance=10kΩ package=THT]
  R2 = Trimmer Potentiometer [maximum_resistance=10kΩ package=THT]
  R5 = Trimmer Potentiometer [maximum_resistance=10kΩ package=THT]
  R6 = Trimmer Potentiometer [maximum_resistance=10kΩ package=THT]
  R3 = Trimmer Potentiometer [maximum_resistance=10kΩ package=THT]
  R4 = Trimmer Potentiometer [maximum_resistance=10kΩ package=THT]
  R15 = Trimmer Potentiometer [maximum_resistance=10kΩ package=THT]
  R14 = Trimmer Potentiometer [maximum_resistance=10kΩ package=THT]
  S13 = Momentary Switch [package=ksa_sealed_tac_switch]
  J19 = HC-SR-04 Connector [form="♀ (female)" package=THT]
  J20 = HC-SR-04 Connector [form="♀ (female)" package=THT]
  J21 = female pin header, 2 pins [form="♀ (female)"]
  J22 = female pin header, 2 pins [form="♀ (female)"]
  J23 = HC-SR-04 Connector [form="♀ (female)" package=THT]
  J24 = female pin header, 2 pins [form="♀ (female)"]
  J25 = female pin header, 2 pins [form="♀ (female)"]
  J26 = HC-SR-04 Connector [form="♀ (female)" package=THT]
  J27 = female pin header, 2 pins [form="♀ (female)"]
  J28 = female pin header, 1 pin [form="♀ (female)"]
  J29 = female pin header, 1 pin [form="♀ (female)"]
  J30 = female pin header, 1 pin [form="♀ (female)"]
  J31 = female pin header, 1 pin [form="♀ (female)"]
  J32 = female pin header, 1 pin [form="♀ (female)"]
  J33 = female pin header, 1 pin [form="♀ (female)"]
  J36 = female pin header, 1 pin [form="♀ (female)"]
  J37 = female pin header, 1 pin [form="♀ (female)"]
  J38 = female pin header, 8 pins [form="♀ (female)"]
  J39 = female pin header, 6 pins [form="♀ (female)"]
  J35 = female pin header, 2 pins [form="♀ (female)"]
  J34 = female pin header, 2 pins [form="♀ (female)"]
  R12 = Resistor [tolerance=±5% resistance=470 package=THT]

nets:
  N1: IC1.OUT1, LED2.anode, Part1.D25
  N2: IC1.IN1-, J31.pin1
  N3: IC1.IN1+, R2.wiper
  VCC: IC1.V+, Part1.5V, Part1.D35, L293D1.+V, J10.VO+, R13.Pin_1, LCD1.VDD, R16.Pin_1, IC2.V+, J13.pin3, J15.Vcc, R1.leg2, R2.leg2, R5.leg2, R6.leg2, R3.leg2, R4.leg2, R14.leg2, J19.Vcc, J23.Vcc, J26.Vcc
  N4: IC1.IN2+, R1.wiper
  N5: IC1.IN2-, J30.pin1
  N6: IC1.OUT2, LED1.anode, Part1.D23
  N7: IC1.OUT3, Part1.D29
  N8: IC1.IN3-, J35.pin1
  N9: IC1.IN3+, J35.pin2
  N10: IC1.GND, R7.Pin_1, R8.Pin_1, R9.Pin_0, R10.Pin_0, R11.Pin_0, R5.leg1, R6.leg1, J27.pin1, R12.Pin_0
  N11: IC1.IN4+, R5.wiper
  N12: IC1.IN4-, J32.pin1
  N13: IC1.OUT4, LED3.anode, Part1.D27
  N14: LED1.cathode, R9.Pin_1
  N15: LED2.cathode, R7.Pin_0
  N16: LED3.cathode, R8.Pin_0
  N17: LED4.cathode, R12.Pin_1
  N18: LED4.anode, Part1.D49, IC2.OUT1
  N19: LED5.cathode, R11.Pin_1
  N20: LED5.anode, Part1.D51, IC2.OUT4
  N21: LED6.cathode, R10.Pin_1
  N22: LED6.anode, Part1.D53, IC2.OUT3
  N23: Part1.A8, J38.pin8
  N24: Part1.A9, J38.pin7
  N25: Part1.A10, J38.pin6
  N26: Part1.A11, J38.pin5
  N27: Part1.A12, J38.pin4
  N28: Part1.A13, J38.pin3
  N29: Part1.A14, J38.pin2
  N30: Part1.A15, J38.pin1
  N31: Part1.A0, S10.2, S10.4
  N32: Part1.A1, S8.1, S8.3
  N33: Part1.D21/SCL, Part1.SCL, J39.pin1
  N34: Part1.D20/SDA, Part1.SDA, J39.pin2
  N35: Part1.D19/RX1, J39.pin3
  N36: Part1.D18/TX1, J39.pin4
  N37: Part1.D17_PWM/RX2, J39.pin5
  N38: Part1.D16_PWM/TX2, J39.pin6
  N39: Part1.D15/RX3, J15.Rx
  N40: Part1.D14/TX3, J15.Tx
  GND: Part1.GND, L293D1.0V, J10.GND, S9.2, LED7.cathode, S10.1, S10.3, LCD1.VSS, LCD1.R/W, LCD1.LED-, S11.2, S8.2, S8.4, S12.1, S12.3, IC2.GND, J15.GND, J17.pin2, J18.pin2, R1.leg1, R2.leg1, R3.leg1, R4.leg1, R14.leg1, S13.1, S13.3, J19.GND, J20.GND, J23.GND, J26.GND, J27.pin2, J29.pin1
  N41: Part1.D12_PWM, L293D1.In_2
  N42: Part1.D10_PWM, L293D1.In_1
  N43: Part1.D9_PWM, L293D1.Enable_1
  N44: Part1.D8_PWM, L293D1.In_4
  N45: Part1.RESET, S9.1
  N46: Part1.D2_PWM, S12.2, S12.4
  N47: Part1.D3_PWM, S11.1
  N48: Part1.D4_PWM, S13.2, S13.4
  N49: Part1.D5_PWM, L293D1.In_3
  N50: Part1.D6_PWM, L293D1.Enable_2
  N51: Part1.D22, LCD1.RS
  N52: Part1.D26, LCD1.E
  N53: Part1.D28, LCD1.DB0, J16.pin1
  N54: Part1.D30, LCD1.DB1, J16.pin2
  N55: Part1.D31, J13.pin1
  N56: Part1.D32, LCD1.DB2, J16.pin3
  N57: Part1.D33, J13.pin2
  N58: Part1.D34, LCD1.DB3, J16.pin4, J28.pin1
  N59: Part1.D36, LCD1.DB4
  N60: Part1.D37, J13.pin4
  N61: Part1.D38, LCD1.DB5
  N62: Part1.D39, J13.pin5
  N63: Part1.D40, LCD1.DB6
  N64: Part1.D41, J13.pin6
  N65: Part1.D42, LCD1.DB7
  N66: Part1.D43, J13.pin7
  N67: Part1.D45, J13.pin8
  N68: Part1.D47, IC2.OUT2
  N69: J8.pin1, L293D1.Out_3_(_Controlled_by_Enable_2_)
  N70: J8.pin2, L293D1.Out_4_(_Controlled_by_Enable_2_)
  N71: J9.pin1, L293D1.Out_1_(_Controlled_by_Enable_1_)
  N72: J9.pin2, L293D1.Out_2_(_Controlled_by_Enable_1_)
  N73: L293D1.+Vmotor, J10.IN+, S6.P
  N74: S6.O, J18.pin1
  N75: LED7.anode, R13.Pin_0, J20.Vcc
  N76: LCD1.V0, R14.wiper
  N77: LCD1.LED+, R15.leg1
  N78: R16.Pin_0, J12.pin1
  N79: J12.pin2, R15.wiper, R15.leg2
  N80: IC2.IN1-, J33.pin1
  N81: IC2.IN1+, R6.wiper
  N82: IC2.IN2+, J34.pin2
  N83: IC2.IN2-, J34.pin1
  N84: IC2.IN3-, J36.pin1
  N85: IC2.IN3+, R4.wiper
  N86: IC2.IN4+, R3.wiper
  N87: IC2.IN4-, J37.pin1
  N88: J15.SET, J17.pin1
  N89: J19.Trig, J22.pin1
  N90: J19.Echo, J22.pin2
  N91: J20.Trig, J21.pin2
  N92: J20.Echo, J21.pin1
  N93: J23.Trig, J24.pin1
  N94: J23.Echo, J24.pin2
  N95: J25.pin1, J26.Echo
  N96: J25.pin2, J26.Trig

custom parts:
  DIP - 14 pins: A DIP stand-in part for whatever IC you want. With 14 pins on a 300mil dual inline package (DIP) footprint.
  Voltage Reguator: 12v-3v3 Adjustable regulator
  HC-12: Transmitter
